// Digital circuit CORE.dig as structural Verilog
module CORE (
  input  CLK_in,
  input  nCLR,
  input  [7:0] IRQ_IN,
  input  MC,
  input  SW,
  input  Go,
  input  Stall,
  output [15:0] PC,
  output [11:0] MIPC,
  output CLK,
  output [7:0] IO_SFR,
  output [7:0] ADDR,
  output nSFR_WE,
  output nSFR_OE,
  output [7:0] nIRQ_CLRB,
  output [7:0] DBUS_inter,
  output IR_WE
);

  wire ALUD_CO, BR_CPLQ, BR_Q, CLK_aync, comparator_1_eq, comparator_1_gt, comparator_1_lt, comparator_2_eq,
       decoder_2_out_0, decoder_2_out_1, decoder_2_out_2, decoder_2_out_3, decoder_2_out_4, decoder_2_out_5,
       decoder_2_out_6, decoder_2_out_7, DPC_JUMP, IRQ_CAI, MIPC_DECVEC, nALUD_CO, nALUDH_OE, nALUDL_OE,
       nALUS_OE, nand_3_out, nDPC_JUMP, nIMMED_OE, nIRQ_OE, nPRRWE, nRAM_OE, nRF_OE, nRFSRCR_WE, nROM_OE,
       nSR_WE, nWR_WE, nXRAM_OE, or_1_out, PFF, RAM_WE, rf_ctl_1_orf_we, RF_SFR, RF_WE, SFR_HIT, XRAM_WE;
  wire [2:0] BR_SRC, BUS_SRC, JUMP_TYPE;
  wire [3:0] ALUSD_FUNC, rf_ctl_1_orf_src, RF_SRC;
  wire [7:0] ADDR_16, IMMED, RF_Q;
  wire [11:0] ADDRESS, multiplexer_1_out;

  BUS_TRAN bus_tran_1 (
    .SFR_HIT(SFR_HIT), .SSFR(RF_SFR), .RAM_WE(RAM_WE), .nRAM_OE(nRAM_OE), .ADDR(ADDR), .BUS_A(DBUS_inter),
    .BUS_B(IO_SFR));
  or or_1 (or_1_out, PFF, Stall);
  PCE PCER (.CLK(CLK), .D(DBUS_inter), .RS(RF_SRC), .WE(RF_WE), .Q(PC));
  assign DBUS_inter = ~nIRQ_OE ? IRQ_IN : 8'bz;  // DriverInvSel driverinvsel_1
  assign DBUS_inter = ~nIMMED_OE ? IMMED : 8'bz;  // DriverInvSel driverinvsel_2
  PullDown #(.Bits(8)) pulldown_1 (.out(DBUS_inter));
  assign DBUS_inter = ~nRF_OE ? RF_Q : 8'bz;  // DriverInvSel driverinvsel_3
  // Probe on DBUS_inter
  STALL u_STALL (
    .Stall(or_1_out), .Go(Go), .nCLR(nCLR), .SW(SW), .CLK_manual(MC), .CLK_in(CLK_in), .CLK(CLK),
    .CLK_async(CLK_aync));
  Multiplexer #(.Bits(12)) multiplexer_1 (
    .sel(MIPC_DECVEC), .in_0(ADDRESS), .in_1({3'b000, DBUS_inter, 1'b1}), .out(multiplexer_1_out));
  Comparator #(.Bits(8)) comparator_1 (
    .a(RF_Q), .b(IMMED), .gt(comparator_1_gt), .eq(comparator_1_eq), .lt(comparator_1_lt));
  CLRIRR clrirr_1 (.D(DBUS_inter), .IRR_CLR(IRQ_CAI), .Q(nIRQ_CLRB));
  DCOUTER #(.generic("Bits := 12;")) dcouter_1 (
    .CLK(CLK), .nCLR(nCLR), .CNT(1'b1), .nLE(nDPC_JUMP), .D(multiplexer_1_out), .Q(MIPC));
  Multiplexer #(.Selector_Bits(3)) multiplexer_2 (
    .sel(JUMP_TYPE), .in_0(1'b0), .in_1(1'b1), .in_2(comparator_1_gt), .in_3(comparator_1_eq),
    .in_4(comparator_1_lt), .in_5(nALUD_CO), .in_6(ALUD_CO), .in_7(BR_Q), .out(DPC_JUMP));
  not not_1 (nDPC_JUMP, DPC_JUMP);
  RF_CTL rf_ctl_1 (
    .CLK(CLK), .BUS_D(DBUS_inter), .RF_SRC(RF_SRC), .RF_WE(RF_WE), .RF_SFR(RF_SFR), .nRFSRCR_WE(nRFSRCR_WE),
    .nRAM_WE(RAM_WE), .nRAM_OE(nRAM_OE), .ORF_SRC(rf_ctl_1_orf_src), .ORF_WE(rf_ctl_1_orf_we),
    .nORF_OE(nRF_OE), .SFR_HIT(SFR_HIT));
  ROM #(.AddrBits(12), .Bits(48)) DECODER (
    .A(MIPC), .sel(1'b1),
    .D({nPRRWE, BUS_SRC, BR_CPLQ, BR_SRC, ALUSD_FUNC, XRAM_WE, RAM_WE, nWR_WE, nSR_WE, IRQ_CAI, nRFSRCR_WE, RF_SFR, RF_WE, RF_SRC, MIPC_DECVEC, JUMP_TYPE, ADDRESS, IMMED}));
  Comparator #(.Bits(4)) comparator_2 (.a(rf_ctl_1_orf_src), .b(4'b1010), .eq(comparator_2_eq));  // open: gt, lt
  nand nand_1 (nSFR_WE, RF_SFR, RAM_WE);
  nand nand_2 (nSFR_OE, RF_SFR, ~nRAM_OE);  // NAnd
  reg_file RF (
    .CLK(CLK), .D(DBUS_inter), .RS(rf_ctl_1_orf_src), .LE(rf_ctl_1_orf_we), .CPF(MIPC_DECVEC), .Q(RF_Q),
    .PFF(PFF));
  and and_1 (IR_WE, comparator_2_eq, rf_ctl_1_orf_we);
  // Probe on MIPC
  // Probe on IMMED
  // Probe on ADDRESS
  // Probe on JUMP_TYPE
  // Probe on MIPC_DECVEC
  // Probe on RF_SRC
  // Probe on RF_WE
  // Probe on RF_SFR
  // Probe on nRFSRCR_WE
  // Probe on nSR_WE
  // Probe on RAM_WE
  // Probe on XRAM_WE
  // Probe on BR_SRC
  // Probe on BR_CPLQ
  // Probe on nWR_WE
  // Probe on ALUSD_FUNC
  // Probe on BUS_SRC
  // Probe on IRQ_CAI
  // Probe on RF_Q
  nand nand_3 (nand_3_out, CLK_aync, XRAM_WE);
  reg__sync_clear #(.generic("Bits := 8;")) WR (.D(DBUS_inter), .CLK(CLK), .CLR(nCLR), .LE(nWR_WE), .Q(ADDR_16));
  reg__sync_clear #(.generic("Bits := 8;")) SR (.D(DBUS_inter), .CLK(CLK), .CLR(nCLR), .LE(nSR_WE), .Q(ADDR));
  Decoder #(.Selector_Bits(3)) decoder_2 (
    .sel(BUS_SRC), .out_0(decoder_2_out_0), .out_1(decoder_2_out_1), .out_2(decoder_2_out_2),
    .out_3(decoder_2_out_3), .out_4(decoder_2_out_4), .out_5(decoder_2_out_5), .out_6(decoder_2_out_6),
    .out_7(decoder_2_out_7));
  not not_2 (nALUS_OE, decoder_2_out_0);
  not not_3 (nALUDL_OE, decoder_2_out_1);
  not not_4 (nALUDH_OE, decoder_2_out_2);
  not not_5 (nRAM_OE, decoder_2_out_3);
  not not_6 (nROM_OE, decoder_2_out_4);
  not not_7 (nXRAM_OE, decoder_2_out_5);
  not not_8 (nIMMED_OE, decoder_2_out_6);
  not not_9 (nIRQ_OE, decoder_2_out_7);
  not not_10 (nALUD_CO, ALUD_CO);
  RAMSinglePortSel #(.AddrBits(16), .Bits(8)) XRAM (
    .A({ADDR, ADDR_16}), .CS(~1'b0), .WE(~nand_3_out), .OE(~nXRAM_OE), .D(DBUS_inter));
  // Probe WRQ on ADDR_16
  // Probe SRQ on ADDR
  ALU ALU (
    .A(RF_Q), .B(ADDR_16), .S(ALUSD_FUNC), .CI(BR_Q), .SOE(nALUS_OE), .DLOE(nALUDL_OE), .DHOE(nALUDH_OE),
    .O(DBUS_inter), .CO(ALUD_CO));
  ROM rom_1 (
    .A({ADDR, ADDR_16}), .nOE(nROM_OE), .IMMED(IMMED), .CLK(CLK), .nPRRWE(nPRRWE), .D(DBUS_inter));  // open: ROM_DB, IPRO_ADDR
  RAM RAM (.CLK(CLK_aync), .A(ADDR), .WE(RAM_WE), .nOE(nRAM_OE), .Dt(RF_SFR), .O(DBUS_inter));
  BR BR (
    .CLK(CLK), .nCLR(nCLR), .S(BR_SRC), .I4(nALUD_CO), .I5(ALUD_CO), .I7(RF_Q[0]), .I6(RF_Q[7]),
    .CPQ(BR_CPLQ), .Q(BR_Q));

  // Other names for the same wires on the sheet: ADDR_16[15:8] = ADDR; ADDR_RAM[7:0] = ADDR; BUS_D[7:0] = DBUS_inter;
  //   BUS_SFRD[7:0] = IO_SFR

  // Notes on the sheet:
  //   PC: program counter's value
  //   MIPC: microinstruction program counter's value
  //   CLK: The CPU main clock
  //   IO_SFR: IO pin connected to peripheral SFR,
  //   It is connected to the internal IO bus 
  //   through a bus transceiver.
  //   ADDR: address used by external SFR
  //   DBUS_inter: IR load value
  //   Stall: stall CPU
  //   LS161
  //   LS151/LS251
  //   contents of DECODER (hex, n*v repeats v):
  //   8140152700,1f295854cd00,1f905914cd00,1f295854ce00,1f905914ce00,1f295854c700,1f905914c700,
  //   1f295854c600,1f905914c600,1f295854c500,1f905914c500,1f295854c000,1f905914c000,1f295854bb00,
  //   1f905914bb00,1f295854bb00,1f905914bb00,1f295854b700,1f905914b700,1f295854b700,1f905914b700,
  //   1f295854b700,1f905914b700,1f295854b700,1f905914b700,1f295854b700,1f905914b700,1f295854b700,
  //   1f905914b700,1f295854b700,1f905914b700,1f295854b700,1f905914b700,1f295854a900,1f905914a900,
  //   1f295854d300,1f905914d300,1f2958549e00,1f9059149e00,1f2958549b00,1f9059149b00,1f2958549a00,
  //   1f9059149a00,1f2958549400,1f9059149400,1f2958548f00,1f9059148f00,1f2958548f00,1f9059148f00,
  //   1f2958548b00,1f9059148b00,1f2958548b00,1f9059148b00,1f2958548b00,1f9059148b00,1f2958548b00,
  //   1f9059148b00,1f2958548b00,1f9059148b00,1f2958548b00,1f9059148b00,1f2958548b00,1f9059148b00,
  //   1f2958548b00,1f9059148b00,1f2958548000,1f9059148000,1f295854ce00,1f905914ce00,1f2958547b00,
  //   1f9059147b00,1f2958547a00,1f9059147a00,1f2958547300,1f9059147300,1f2958546900,1f9059146900,
  //   1f2958545f00,1f9059145f00,1f2958545f00,1f9059145f00,1f2958545600,1f9059145600,1f2958545600,
  //   1f9059145600,1f2958545600,1f9059145600,1f2958545600,1f9059145600,1f2958545600,1f9059145600,
  //   1f2958545600,1f9059145600,1f2958545600,1f9059145600,1f2958545600,1f9059145600,1f2958544b00,
  //   1f9059144b00,1f295854d300,1f905914d300,1f2958544500,1f9059144500,1f2958544200,1f9059144200,
  //   1f2958543a00,1f9059143a00,1f2958542f00,1f9059142f00,1f2958542500,1f9059142500,1f2958542500,
  //   1f9059142500,1f2958541c00,1f9059141c00,1f2958541c00,1f9059141c00,1f2958541c00,1f9059141c00,
  //   1f2958541c00,1f9059141c00,1f2958541c00,1f9059141c00,1f2958541c00,1f9059141c00,1f2958541c00,
  //   1f9059141c00,1f2958541c00,1f9059141c00,1f2958541900,1f9059141900,1f295854ce00,1f905914ce00,
  //   1f2958541400,1f9059141400,1f2958540b00,1f9059140b00,1f2958540900,1f9059140900,1f2958540500,
  //   1f9059140500,1f2958540000,1f9059140000,1f2958540000,1f9059140000,1f295853fc00,1f905913fc00,
  //   1f295853fc00,1f905913fc00,1f295853fc00,1f905913fc00,1f295853fc00,1f905913fc00,1f295853fc00,
  //   1f905913fc00,1f295853fc00,1f905913fc00,1f295853fc00,1f905913fc00,1f295853fc00,1f905913fc00,
  //   1f295853f900,1f905913f900,1f295854d300,1f905914d300,1f295853f400,1f905913f400,1f295853eb00,
  //   1f905913eb00,1f295853e900,1f905913e900,1f295853e500,1f905913e500,1f295853e000,1f905913e000,
  //   1f295853e000,1f905913e000,1f295853dc00,1f905913dc00,1f295853dc00,1f905913dc00,1f295853dc00,
  //   1f905913dc00,1f295853dc00,1f905913dc00,1f295853dc00,1f905913dc00,1f295853dc00,1f905913dc00,
  //   1f295853dc00,1f905913dc00,1f295853dc00,1f905913dc00,1f295853d900,1f905913d900,1f295854ce00,
  //   1f905914ce00,1f295853d400,1f905913d400,1f295853cb00,1f905913cb00,1f295853c900,1f905913c900,
  //   1f295853c500,1f905913c500,1f295853c000,1f905913c000,1f295853c000,1f905913c000,1f295853bc00,
  //   1f905913bc00,1f295853bc00,1f905913bc00,1f295853bc00,1f905913bc00,1f295853bc00,1f905913bc00,
  //   1f295853bc00,1f905913bc00,1f295853bc00,1f905913bc00,1f295853bc00,1f905913bc00,1f295853bc00,
  //   1f905913bc00,1f295853b900,1f905913b900,1f295854d300,1f905914d300,1f295853b000,1f905913b000,
  //   1f295853ab00,1f905913ab00,1f295853aa00,1f905913aa00,1f295853a300,1f905913a300,1f2958539e00,
  //   1f9059139e00,1f2958539e00,1f9059139e00,1f2958539a00,1f9059139a00,1f2958539a00,1f9059139a00,
  //   1f2958539a00,1f9059139a00,1f2958539a00,1f9059139a00,1f2958539a00,1f9059139a00,1f2958539a00,
  //   1f9059139a00,1f2958539a00,1f9059139a00,1f2958539a00,1f9059139a00,1f2958539500,1f9059139500,
  //   1f295854ce00,1f905914ce00,1f2958538c00,1f9059138c00,1f2958538800,1f9059138800,1f2958535600,
  //   1f9059135600,1f2958534c00,1f9059134c00,1f2958534400,1f9059134400,1f2958534400,1f9059134400,
  //   1f2958533d00,1f9059133d00,1f2958533d00,1f9059133d00,1f2958533d00,1f9059133d00,1f2958533d00,
  //   1f9059133d00,1f2958533d00,1f9059133d00,1f2958533d00,1f9059133d00,1f2958533d00,1f9059133d00,
  //   1f2958533d00,1f9059133d00,1f2958533900,1f9059133900,1f295854d300,1f905914d300,1f2958533000,
  //   1f9059133000,1f2958532c00,1f9059132c00,1f2958532400,1f9059132400,1f2958531900,1f9059131900,
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  //   LS137/LS138
  //   core is at28c64
  //   at28c64
  //   core is 6116
  //   L74+LS252
endmodule
